# Fritzing sketch Wiring (saved by Fritzing 1.0.4)

parts:
  A1 = XY-3606
  TB6600 = IC, SIP package, 12 pins [chip_label=TB6600]
  Raspberry_Pi_1 = Raspberry Pi 3 [part_number=RPI-3-V1.2]
  TB6601 = IC, SIP package, 12 pins [chip_label=TB6600]
  M2 = Stepper Motor - Bipolar
  M3 = Stepper Motor - Bipolar

nets:
  12V: A1.Pin_1, TB6600.pin12, TB6601.pin12
  GND: A1.Pin_2, A1.Pin_3, TB6600.pin11, Raspberry_Pi_1.GND, TB6601.pin3, TB6601.pin5, TB6601.pin11
  N1: A1.Pin_4, Raspberry_Pi_1.5V
  N2: TB6600.pin3, TB6600.pin5
  N3: TB6600.pin4, Raspberry_Pi_1.GIPO27
  N4: TB6600.pin6, Raspberry_Pi_1.GIPO17
  N5: TB6600.pin7, M2.D
  N6: TB6600.pin8, M2.B
  N7: TB6600.pin9, M2.C
  N8: TB6600.pin10, M2.A
  N9: Raspberry_Pi_1.GIPO24, TB6601.pin4
  N10: Raspberry_Pi_1.GIPO23, TB6601.pin6
  N11: TB6601.pin7, M3.D
  N12: TB6601.pin8, M3.B
  N13: TB6601.pin9, M3.C
  N14: TB6601.pin10, M3.A

custom parts:
  XY-3606: 24V/12V turn 5V 5A power module, DC-DC XY-3606 Power Converter Super LM2596S.
